# Fritzing sketch USBasp+ (saved by Fritzing 0.9.3b)
circuit board: 8.49773cm x 6.14135cm
breadboards: 1

parts:
  12MHz = Crystal [frequency="16 MHz" package=SMD]
  U1 = USB+SHIELD [package=usb-b-pth]
  R1 = Resistor [tolerance=±5% resistance=10k package=THT]
  C1 = Ceramic Capacitor [capacitance=22pF package="100 mil [THT, multilayer]"]
  R3 = Resistor [tolerance=±5% resistance=1k package=THT]
  R2 = Resistor [tolerance=±5% resistance=1k package=THT]
  LED1 = LED - 3mm [color="Green (570nm)" package="3 mm [THT]"]
  LED2 = LED - 3mm [color="Red (633nm)" package="3 mm [THT]"]
  D1 = Rectifier Diode [part_number=1N4001 package="300 mil [THT]"]
  D2 = Rectifier Diode [part_number=1N4001 package="300 mil [THT]"]
  R4 = Resistor [tolerance=±5% resistance=68 package=THT]
  R5 = Resistor [tolerance=±5% resistance=68 package=THT]
  ATMega8 = MICROCONTROLLER [package=dil28-3-zif_socket]
  C2 = Ceramic Capacitor [capacitance=22pF package="100 mil [THT, multilayer]"]

nets:
  N1: 12MHz.pin_0, ATMega8.PB7(XTAL2_TOSC2), C2.1
  N2: 12MHz.pin_1, C1.1, ATMega8.PB6(XTAL1_TOSC1)
  N3: U1.D+, D1.cathode, R5.Pin_1
  N4: U1.D-, D2.cathode, R4.Pin_1
  GND: U1.GND, C1.0, D1.anode, D2.anode, ATMega8.GND, ATMega8.AGND, C2.0
  N5: U1.VBUS, R1.Pin_0, R3.Pin_0, R2.Pin_0, ATMega8.VCC, ATMega8.AVCC
  N6: R1.Pin_1, ATMega8.PC6(_RESET)
  N7: R3.Pin_1, LED2.cathode
  N8: R2.Pin_1, LED1.cathode
  N9: LED1.anode, ATMega8.PC0(ADC0)
  N10: LED2.anode, ATMega8.PC1(ADC1)
  N11: R4.Pin_0, ATMega8.PB0(ICP)
  N12: R5.Pin_0, ATMega8.PB1(OC1A)
